# Fritzing sketch Preliminary Vero board circuit (saved by Fritzing 0.9.3b)
stripboards: 1

parts:
  IC1 = IC, DIP package, 8 pins [chip_label=MCP3202]
  C1 = Electrolytic Capacitor [capacitance=1mF package="100 mil [THT, electrolytic]"]
  Raspberry_Pi_Zero1 = Raspberry Pi Zero
  R1 = Resistor [tolerance=±5% resistance=1k package=THT]
  R2 = Resistor [tolerance=±5% resistance=2.2k package=THT]
  R3 = Resistor [tolerance=±5% resistance=1k package=THT]
  U1 = Transformer [package=transformer]
  U2 = Transformer [package=transformer_smd]
  C2 = Electrolytic Capacitor [capacitance=1mF package="100 mil [THT, electrolytic]"]
  R4 = Resistor [tolerance=±5% resistance=50 package=THT]
  R5 = Resistor [tolerance=±5% resistance=100 package=THT]
  R6 = Resistor [tolerance=±5% resistance=100 package=THT]
  Q1 = PNP-Transistor [package="TO92 [THT]"]
  R7 = Resistor [tolerance=±5% resistance=10k package=THT]
  R8 = Resistor [tolerance=±5% resistance=1k package=THT]
  U5 = RELAY-2 [package=relay-g5v]
  D1 = Rectifier Diode [part_number=1N4001 package="300 mil [THT]"]

nets:
  N1: IC1.pin1, Raspberry_Pi_Zero1.GPIO8
  N2: IC1.pin2, R1.Pin_1, R2.Pin_1, R3.Pin_0
  N3: IC1.pin3, R4.Pin_1, R5.Pin_1, R6.Pin_0
  N4: IC1.pin4, Raspberry_Pi_Zero1.GND, R3.Pin_1, U1.3, U2.4, R6.Pin_1, Q1.E, R8.Pin_1
  N5: IC1.pin5, Raspberry_Pi_Zero1.GPIO9
  N6: IC1.pin6, Raspberry_Pi_Zero1.GPIO10
  N7: IC1.pin7, Raspberry_Pi_Zero1.GPIO11
  N8: IC1.pin8, Raspberry_Pi_Zero1.5V, R1.Pin_0, R5.Pin_0, U5.6, D1.cathode
  N9: C1.-, R2.Pin_0
  N10: C1.+, U1.2
  N11: Raspberry_Pi_Zero1.GPIO21, R7.Pin_1
  N12: U2.3, C2.+
  N13: C2.-, R4.Pin_0
  N14: Q1.B, R7.Pin_0, R8.Pin_0
  N15: Q1.C, U5.5, D1.anode
  N16: U5.1, U5.10
  N17: U5.2, U5.9
